# Fritzing sketch receiver (saved by Fritzing 0.9.2b)
circuit board: 2.1549cm x 3.58523cm
breadboards: 1

parts:
  RJ45 = RJ45 Jack [package=rj45-8]
  R1 = Resistor [tolerance=±5% resistance=220 package=THT]
  R2 = Resistor [tolerance=±5% resistance=220 package=THT]
  R3 = Resistor [tolerance=±5% resistance=220 package=THT]
  MAX485 = MAX485 [package=dil08]
  R-7850 = Voltage Regulator - 5V [package="TO220 [THT]"]
  LED = Header 3 [package=molex-1x3_lock]
  R4 = Resistor [package=THT]

nets:
  N1: RJ45.1, R1.Pin_1, R2.Pin_1, MAX485.A
  N2: RJ45.2, R2.Pin_0, R3.Pin_0, MAX485.B
  N3: RJ45.4, RJ45.6, RJ45.8, R-7850.input_voltage
  N4: R3.Pin_1, MAX485.VCC, R-7850.output_voltage, LED.1
  N5: MAX485.RO, R4.pin_0
  N6: LED.3, R4.pin_1

custom parts:
  Resistor: A generic resistor
